# Fritzing sketch fritzing (saved by Fritzing 0.9.3b)
breadboards: 1

parts:
  LED1 = LED - 5mm [color="Red (633nm)" package="5 mm [THT]"]  # not connected
  R1 = Resistor [tolerance=±5% resistance=330 package=THT]  # not connected
  S1 = Square Pushbutton
  R2 = Resistor [tolerance=±5% resistance=33k package=THT]
  Componente1 = Arduino Uno (Rev3)

nets:
  N1: S1.leg0, Componente1.5V
  N2: S1.leg1, R2.Pin_1, Componente1.D2
